// Logisim project Lab-4-Given.circ as structural Verilog: 12 circuits, main circuit Main
module Main (
);

  wire ALUSrc, Branch, Clock, ex_mem_1_aluop0_2, ex_mem_1_aluop1_2, ex_mem_1_aluop2_2, ex_mem_1_aluop3_2,
       ex_mem_1_alusrc_2, ex_mem_1_branch_2, ex_mem_1_jal_2, ex_mem_1_jr_2, ex_mem_1_jump_2,
       ex_mem_1_memtoreg_2, ex_mem_1_regdest_2, EX_MEM_RegWrite, hazard_detection_1_stalling,
       id_ex_1_memtoreg_2, id_ex_1_memwrite_2, id_ex_1_regdest_2, id_ex_1_regwrite_2, ID_EX_MemRead,
       IF_ID_Write, JAL, JR, Jump, MemForward, MemRead, MemtoReg, MemWrite, MemWriteDec, or_2_out, PCSrc,
       PCWrite, RegWrite, Squish, Squish_Fetch, Stall_Control, Zero, ZeroR;
  wire [1:0] FA, FB;
  wire [3:0] ALUCtrl;
  wire [4:0] EX_MEM_Rd, id_ex_1__11_15_2, ID_EX_Rt, multiplexer_4_out, multiplexer_7_out, RS, shift, WrAddr;
  wire [5:0] _0_5, _26_31;
  wire [13:0] control_unit_1_flags, multiplexer_2_out;
  wire [15:6] _0_15;
  wire [25:0] J_Offset;
  wire [25:16] _0_25;
  wire [31:0] A, alu_1_aluresult, ALUAdd, ALUout, B, bit_extender_1_out, Data, Forwarding, Immediate,
       mem_wb_1_alu_2, mem_wb_1_data_2, MemData, multiplexer_1_out, multiplexer_6_out, multiplexer_8_out,
       multiplexer_11_out, PC_4, PC___l1, PC___l2, PC_d, PC_d_saved, PC_q, PCin, RD, RD1, RD2, rom_1_data,
       shifter_1_out, WrData;

  Clock clock_1 (.out(Clock));
  Multiplexer #(.width(32)) multiplexer_1 (
    .in0(PCin), .in1(Forwarding), .out(multiplexer_1_out), .sel(JR));  // open: en
  Register #(.width(32)) PC (.D(multiplexer_1_out), .en(PCWrite), .Q(PC_q), .clk(Clock));  // open: clr
  or or_1 (Squish, Jump, JR, PCSrc);
  Adder #(.width(32)) adder_1 (.a(PC_q), .b(32'h4), .out(PC_4));  // open: cin, cout
  ROM #(.dataWidth(32)) rom_1 (.addr(PC_q[9:2]), .data(rom_1_data));  // open: sel
  // Probe on rom_1_data
  IF_ID if_id_1 (
    .PC(PC_4), .IRin(rom_1_data), .PC_2(PC_d), .IRout({_26_31, _0_25, _0_15, _0_5}), .Clock(Clock),
    .notNOP(IF_ID_Write), .Squish(Squish), .Squish_2(Squish_Fetch));
  // Probe on {_26_31, _0_25, _0_15, _0_5}
  // Probe on WrAddr
  // Probe on WrData
  // Probe on _0_25[20:16]
  // Probe on _0_25[25:21]
  // Probe on _26_31
  // Probe on _0_5
  Register_File register_file_1 (
    .WrAddr(WrAddr), .WrData(WrData), .WrReg(RegWrite), .RdAddr1(_0_25[25:21]), .RdAddr2(_0_25[20:16]),
    .RdData1(RD1), .RdData2(RD2), .Clock(Clock));
  Control_Unit control_unit_1 (.OpCode(_26_31), .Func(_0_5), .Flags(control_unit_1_flags));
  or or_2 (or_2_out, Squish, Squish_Fetch, Stall_Control);
  Multiplexer #(.width(14)) multiplexer_2 (
    .in0(control_unit_1_flags), .in1({14{1'b0}}),
    .out({multiplexer_2_out[13:5], MemWriteDec, multiplexer_2_out[3:0]}), .sel(or_2_out));  // open: en
  assign bit_extender_1_out = {{16{_0_15[15]}}, {_0_15, _0_5}};  // Bit_Extender bit_extender_1
  Hazard_Detection hazard_detection_1 (
    .ID_EX_MemRead(ID_EX_MemRead), .ID_EX_Rt(ID_EX_Rt), .IF_ID_Rs(_0_25[25:21]), .IF_ID_Rt(_0_25[20:16]),
    .MemWrite_Dec(MemWriteDec), .IF_ID_Write(IF_ID_Write), .PCWrite(PCWrite), .Stall_Control(Stall_Control),
    .Stalling(hazard_detection_1_stalling));
  // Probe on hazard_detection_1_stalling
  ID_EX id_ex_1 (
    .ALUOp3(multiplexer_2_out[13]), .ALUOp2(multiplexer_2_out[12]), .ALUOp1(multiplexer_2_out[11]),
    .ALUOp0(multiplexer_2_out[10]), .RegDest(multiplexer_2_out[9]), .Jump(multiplexer_2_out[8]),
    .Branch(multiplexer_2_out[7]), .MemRead(multiplexer_2_out[6]), .MemtoReg(multiplexer_2_out[5]),
    .MemWrite(MemWriteDec), .ALUSrc(multiplexer_2_out[3]), .RegWrite(multiplexer_2_out[2]),
    .JR(multiplexer_2_out[1]), .JAL(multiplexer_2_out[0]), .Clock(Clock), .ALUOp3_2(ALUCtrl[3]),
    .ALUOp2_2(ALUCtrl[2]), .ALUOp1_2(ALUCtrl[1]), .ALUOp0_2(ALUCtrl[0]), .RegDest_2(id_ex_1_regdest_2),
    .Jump_2(Jump), .Branch_2(Branch), .MemRead_2(ID_EX_MemRead), .MemtoReg_2(id_ex_1_memtoreg_2),
    .MemWrite_2(id_ex_1_memwrite_2), .ALUSrc_2(ALUSrc), .RegWrite_2(id_ex_1_regwrite_2), .JR_2(JR),
    .JAL_2(JAL), .PC_d(PC_d), .PC(PC_d_saved), .RD1(RD1), .A(A), .RD1_2(RD2), .B(B),
    .Imm(bit_extender_1_out), ._16_20(_0_25[20:16]), ._16_20_2(ID_EX_Rt), ._11_15(_0_15[15:11]),
    ._11_15_2(id_ex_1__11_15_2), ._6_10(_0_15[10:6]), .shift(shift), ._21_25(_0_25[25:21]), .RS(RS),
    ._0_25({_0_25, _0_15, _0_5}), .Imm_2(Immediate), ._0_25_2(J_Offset));
  // Probe on _0_25[20:16]
  // Probe on _0_15[15:11]
  Multiplexer #(.select(2), .width(32)) multiplexer_3 (
    .in0(B), .in1(WrData), .in2(ALUAdd), .out(RD), .sel(FB));  // open: in3, en
  // Probe on ID_EX_Rt
  // Probe on id_ex_1__11_15_2
  // Probe on multiplexer_4_out
  Multiplexer #(.width(5)) multiplexer_4 (
    .in0(id_ex_1__11_15_2), .in1(ID_EX_Rt), .out(multiplexer_4_out), .sel(id_ex_1_regdest_2));  // open: en
  Multiplexer #(.select(2), .width(32)) multiplexer_5 (
    .in0(A), .in1(WrData), .in2(ALUAdd), .out(Forwarding), .sel(FA));  // open: in3, en
  Multiplexer #(.width(32)) multiplexer_6 (
    .in0(RD), .in1(Immediate), .out(multiplexer_6_out), .sel(ALUSrc));  // open: en
  Multiplexer #(.width(5)) multiplexer_7 (
    .in0(multiplexer_4_out), .in1({5{1'b1}}), .out(multiplexer_7_out), .sel(JAL));  // open: en
  Shifter #(.width(32)) shifter_1 (.in(Immediate), .\dist (5'b00010), .out(shifter_1_out));
  // Probe on ALUCtrl
  ALU alu_1 (
    .ALUCtl(ALUCtrl), .A(Forwarding), .B(multiplexer_6_out), .ALUResult(alu_1_aluresult), .Zero(Zero),
    .Shamt(shift));  // open: Overflow
  // Probe on RS
  // Probe on EX_MEM_Rd
  Adder #(.width(32)) adder_2 (.a(PC_d_saved), .b(shifter_1_out), .out(PC___l1));  // open: cin, cout
  // Probe on alu_1_aluresult
  and and_1 (PCSrc, Branch, Zero);
  // Probe on ID_EX_Rt
  Forwarding_Unit forwarding_unit_1 (
    .ID_EX_Rs(RS), .ID_EX_Rt(ID_EX_Rt), .EX_MEM_RegWrite(EX_MEM_RegWrite), .EX_MEM_Reg_Rd(EX_MEM_Rd),
    .MEM_WB_RegWrite(RegWrite), .MEM_WB_Reg_Rd(WrAddr), .EX_MEM_MemWrite(MemWrite), .ForwardA(FA),
    .ForwardB(FB), .MemForward(MemForward));
  // Probe on WrAddr
  Multiplexer #(.width(32)) multiplexer_8 (
    .in0(PC_4), .in1(PC___l1), .out(multiplexer_8_out), .sel(PCSrc));  // open: en
  Multiplexer #(.width(32)) multiplexer_9 (
    .in0(alu_1_aluresult), .in1(PC_d_saved), .out(ALUout), .sel(JAL));  // open: en
  // Probe on ALUout
  // Probe on FB
  // Probe on FA
  // Probe on multiplexer_7_out
  // Probe on PCin
  Multiplexer #(.width(32)) multiplexer_10 (
    .in0(multiplexer_8_out), .in1({PC_d_saved[31:28], J_Offset, 2'b00}), .out(PCin), .sel(Jump));  // open: en
  EX_MEM ex_mem_1 (
    .Clock(Clock), .ALUOp3(ALUCtrl[3]), .ALUOp3_2(ex_mem_1_aluop3_2), .ALUOp2(ALUCtrl[2]),
    .ALUOp2_2(ex_mem_1_aluop2_2), .ALUOp1(ALUCtrl[1]), .ALUOp1_2(ex_mem_1_aluop1_2), .ALUOp0(ALUCtrl[0]),
    .ALUOp0_2(ex_mem_1_aluop0_2), .RegDest(id_ex_1_regdest_2), .RegDest_2(ex_mem_1_regdest_2), .Jump(Jump),
    .Jump_2(ex_mem_1_jump_2), .Branch(Branch), .Branch_2(ex_mem_1_branch_2), .MemRead(ID_EX_MemRead),
    .MemRead_2(MemRead), .MemtoReg(id_ex_1_memtoreg_2), .MemtoReg_2(ex_mem_1_memtoreg_2),
    .MemWrite(id_ex_1_memwrite_2), .MemWrite_2(MemWrite), .ALUSrc(ALUSrc), .ALUSrc_2(ex_mem_1_alusrc_2),
    .RegWrite(id_ex_1_regwrite_2), .RegWrite_2(EX_MEM_RegWrite), .JR(JR), .JR_2(ex_mem_1_jr_2), .JAL(JAL),
    .JAL_2(ex_mem_1_jal_2), .PC(PC___l1), .PC_2(PC___l2), .ALU(ALUout), .ALU_2(ALUAdd), .RD(RD),
    .RD_2(MemData), .zero(Zero), .zero_2(ZeroR), .dest(multiplexer_7_out), .dest_2(EX_MEM_Rd));
  // Probe on EX_MEM_Rd
  // Probe on {_26_31, _0_25, _0_15, _0_5}
  Multiplexer #(.width(32)) multiplexer_11 (
    .in0(MemData), .in1(WrData), .out(multiplexer_11_out), .sel(MemForward));  // open: en
  MEM_WB mem_wb_1 (
    .ALUOp3(ex_mem_1_aluop3_2), .ALUOp2(ex_mem_1_aluop2_2), .ALUOp1(ex_mem_1_aluop1_2),
    .ALUOp0(ex_mem_1_aluop0_2), .RegDest(ex_mem_1_regdest_2), .Jump(ex_mem_1_jump_2),
    .Branch(ex_mem_1_branch_2), .MemRead(MemRead), .MemtoReg(ex_mem_1_memtoreg_2), .MemWrite(MemWrite),
    .ALUSrc(ex_mem_1_alusrc_2), .RegWrite(EX_MEM_RegWrite), .JR(ex_mem_1_jr_2), .JAL(ex_mem_1_jal_2),
    .MemtoReg_2(MemtoReg), .RegWrite_2(RegWrite), .Clock(Clock), .Data(Data), .Data_2(mem_wb_1_data_2),
    .ALU(ALUAdd), .ALU_2(mem_wb_1_alu_2), .WrAddr(EX_MEM_Rd), .WrAddr_2(WrAddr));  // open: ALUOp3_2, ALUOp2_2, ALUOp1_2, ALUOp0_2, RegDest_2, Jump_2, Branch_2, MemRead_2, MemWrite_2, ALUSrc_2, JR_2, JAL_2
  // Probe on WrAddr
  // Probe on ALUAdd[7:0]
  // Probe on multiplexer_11_out
  Multiplexer #(.width(32)) multiplexer_12 (
    .in0(mem_wb_1_alu_2), .in1(mem_wb_1_data_2), .out(WrData), .sel(MemtoReg));  // open: en
  // Probe on Data
  RAM #(.dataWidth(32), .bus("separate")) ram_1 (
    .addr(ALUAdd[7:0]), .din(multiplexer_11_out), .data(Data), .str(MemWrite), .clk(Clock), .ld(MemRead));  // open: sel, clr
  // Probe on nothing
  // Probe on nothing
  // Probe on nothing
  // Probe on nothing
  // Probe on nothing
  // Probe on nothing
  // Probe on nothing
  // Probe on nothing
  // Probe on nothing
  // Probe on nothing

  // Other names for the same wires on the sheet: _0_15[5:0] = _0_5; _0_25[15:0] = {_0_15, _0_5};
  //   Decode[31:0] = {_26_31, _0_25, _0_15, _0_5}; _6_10[4:0] = _0_15[10:6]; _11_15[4:0] = _0_15[15:11];
  //   _16_20[4:0] = _0_25[20:16]; IF_ID_Rt[4:0] = _0_25[20:16]; _21_25[4:0] = _0_25[25:21];
  //   IF_ID_Rs[4:0] = _0_25[25:21]; notNOP = IF_ID_Write

  // Notes on the sheet:
  //   contents of rom_1 (hex, n*v repeats v):
  //   20010001 2002ffff 34030003 34040004 20050005 20060006 20070007 ac01000c 224020 8c6f0009 224824
  //   825022 a35825 e66026 a6682a c2702b 30300001 18a80 79082
  //   Control Unit generates the flags for the rest
  //   If  JAL, send to R31
  //   Offset for J-type instructions
  //   Might need to switch 16/11 mux
endmodule

module _32_Bit_Adder___Subtractor (
  input  Add_Sub_control,
  input  [31:0] in_2,
  input  [31:0] in_3,
  output [31:0] out_4,
  output carry_out
);

  wire adder_1_cout, subtractor_1_bout;
  wire [31:0] adder_1_out, subtractor_1_out;

  Adder #(.width(32)) adder_1 (.a(in_2), .b(in_3), .out(adder_1_out), .cout(adder_1_cout));  // open: cin
  Subtractor #(.width(32)) subtractor_1 (
    .a(in_2), .b(in_3), .out(subtractor_1_out), .bout(subtractor_1_bout));  // open: bin
  Multiplexer #(.width(32), .enable("false")) multiplexer_1 (
    .in0(adder_1_out), .in1(subtractor_1_out), .out(out_4), .sel(Add_Sub_control));
  Multiplexer #(.enable("false")) multiplexer_2 (
    .in0(adder_1_cout), .in1(subtractor_1_bout), .out(carry_out), .sel(Add_Sub_control));
endmodule

module ALU (
  input  [3:0] ALUCtl,
  input  [31:0] A,
  input  [31:0] B,
  input  [4:0] Shamt,
  output [31:0] ALUResult,
  output Zero,
  output Overflow
);

  wire comparator_1_lt, comparator_2_lt, comparator_3_eq, comparator_4_eq, or_2_out;
  wire [31:0] Add, And, LessThan, LessThanUnsigned, Nor, Or, ShiftLeft, ShiftRight, Sub, Xor;

  assign Xor = A ^ B;  // XOR_Gate xor_1, 32 bits wide
  Adder #(.width(32)) adder_1 (.a(A), .b(B), .out(Add));  // open: cin, cout
  Subtractor #(.width(32)) subtractor_1 (.a(A), .b(B), .out(Sub));  // open: bin, bout
  assign And = A & B;  // AND_Gate and_1, 32 bits wide
  assign Or = A | B;  // OR_Gate or_1, 32 bits wide
  assign Nor = ~(A | B);  // NOR_Gate nor_1, 32 bits wide
  Comparator #(.width(32)) comparator_1 (.a(A), .b(B), .lt(comparator_1_lt));  // open: gt, eq
  assign LessThan = {{31{1'b0}}, comparator_1_lt};  // Bit_Extender bit_extender_1
  Shifter #(.width(32)) shifter_1 (.in(B), .\dist (Shamt), .out(ShiftLeft));
  Shifter #(.width(32), .shift("lr")) shifter_2 (.in(B), .\dist (Shamt), .out(ShiftRight));
  Comparator #(.width(32), .mode("unsigned")) comparator_2 (.a(A), .b(B), .lt(comparator_2_lt));  // open: gt, eq
  assign LessThanUnsigned = {{31{1'b0}}, comparator_2_lt};  // Bit_Extender bit_extender_2
  Multiplexer #(.select(4), .width(32), .enable("false")) multiplexer_1 (
    .in0(Or), .in1(LessThanUnsigned), .in2(LessThan), .in3(Add), .in4(Sub), .in5(Xor), .in6(And),
    .in14(ShiftRight), .in15(ShiftLeft), .out(ALUResult), .sel(ALUCtl));  // open: in7, in8, in9, in10, in11, in12, in13
  Comparator #(.width(4)) comparator_3 (.a(4'b0011), .b(ALUCtl), .eq(comparator_3_eq));  // open: gt, lt
  Comparator #(.width(4)) comparator_4 (.a(ALUCtl), .b(4'b0100), .eq(comparator_4_eq));  // open: gt, lt
  Overflow_Unit overflow_unit_1 (
    .Add(comparator_3_eq), .Sub(comparator_4_eq), .ASign(A[31]), .BSign(B[31]), .ResultSign(ALUResult[31]),
    .Overflow(Overflow));
  not not_1 (Zero, or_2_out);
  or or_2 (or_2_out, ALUResult[0], ALUResult[1], ALUResult[2], ALUResult[3], ALUResult[4], ALUResult[5], ALUResult[6], ALUResult[7], ALUResult[8], ALUResult[9], ALUResult[10], ALUResult[11], ALUResult[12], ALUResult[13], ALUResult[14], ALUResult[15], ALUResult[16], ALUResult[17], ALUResult[18], ALUResult[19], ALUResult[20], ALUResult[21], ALUResult[22], ALUResult[23], ALUResult[24], ALUResult[25], ALUResult[26], ALUResult[27], ALUResult[28], ALUResult[29], ALUResult[30], ALUResult[31]);

  // Other names for the same wires on the sheet: ASign = A[31]; ResultSign = ALUResult[31]; BSign = B[31]
endmodule

module Register_File (
  input  [4:0] WrAddr,
  input  [31:0] WrData,
  input  WrReg,
  input  [4:0] RdAddr1,
  input  [4:0] RdAddr2,
  input  Clock,
  output [31:0] RdData1,
  output [31:0] RdData2
);

  wire and_1_out, and_2_out, comparator_1_eq, comparator_2_eq, comparator_3_eq, comparator_4_eq, not_1_out,
       not_2_out, WrReg0, WrReg1, WrReg2, WrReg3, WrReg4, WrReg5, WrReg6, WrReg7, WrReg8, WrReg9, WrReg10,
       WrReg11, WrReg12, WrReg13, WrReg14, WrReg15, WrReg16, WrReg17, WrReg18, WrReg19, WrReg20, WrReg21,
       WrReg22, WrReg23, WrReg24, WrReg25, WrReg26, WrReg27, WrReg28, WrReg29, WrReg30, WrReg31;
  wire [31:0] multiplexer_1_out, multiplexer_2_out, RegData1, RegData2, RegData3, RegData4, RegData5,
       RegData6, RegData7, RegData8, RegData9, RegData10, RegData11, RegData12, RegData13, RegData14,
       RegData15, RegData16, RegData17, RegData18, RegData19, RegData20, RegData21, RegData22, RegData23,
       RegData24, RegData25, RegData26, RegData27, RegData28, RegData29, RegData30, RegData31;

  Demultiplexer #(.select(5), .enable("false")) demultiplexer_1 (
    .out0(WrReg0), .out1(WrReg1), .out2(WrReg2), .out3(WrReg3), .out4(WrReg4), .out5(WrReg5), .out6(WrReg6),
    .out7(WrReg7), .out8(WrReg8), .out9(WrReg9), .out10(WrReg10), .out11(WrReg11), .out12(WrReg12),
    .out13(WrReg13), .out14(WrReg14), .out15(WrReg15), .out16(WrReg16), .out17(WrReg17), .out18(WrReg18),
    .out19(WrReg19), .out20(WrReg20), .out21(WrReg21), .out22(WrReg22), .out23(WrReg23), .out24(WrReg24),
    .out25(WrReg25), .out26(WrReg26), .out27(WrReg27), .out28(WrReg28), .out29(WrReg29), .out30(WrReg30),
    .out31(WrReg31), .in(WrReg), .sel(WrAddr));
  // Probe on RegData4
  Register #(.width(32)) Reg4 (.D(WrData), .en(WrReg4), .Q(RegData4), .clk(Clock));  // open: clr
  // Probe on RegData8
  Register #(.width(32)) Reg8 (.D(WrData), .en(WrReg8), .Q(RegData8), .clk(Clock));  // open: clr
  // Probe on RegData12
  Register #(.width(32)) Reg12 (.D(WrData), .en(WrReg12), .Q(RegData12), .clk(Clock));  // open: clr
  // Probe on RegData16
  Register #(.width(32)) Reg16 (.D(WrData), .en(WrReg16), .Q(RegData16), .clk(Clock));  // open: clr
  // Probe on RegData20
  Register #(.width(32)) Reg20 (.D(WrData), .en(WrReg20), .Q(RegData20), .clk(Clock));  // open: clr
  // Probe on RegData24
  Register #(.width(32)) Reg24 (.D(WrData), .en(WrReg24), .Q(RegData24), .clk(Clock));  // open: clr
  // Probe on RegData28
  Register #(.width(32)) Reg28 (.D(WrData), .en(WrReg28), .Q(RegData28), .clk(Clock));  // open: clr
  Register #(.width(32)) Reg1 (.D(WrData), .en(WrReg1), .Q(RegData1), .clk(Clock));  // open: clr
  Register #(.width(32)) Reg5 (.D(WrData), .en(WrReg5), .Q(RegData5), .clk(Clock));  // open: clr
  Register #(.width(32)) Reg9 (.D(WrData), .en(WrReg9), .Q(RegData9), .clk(Clock));  // open: clr
  Register #(.width(32)) Reg13 (.D(WrData), .en(WrReg13), .Q(RegData13), .clk(Clock));  // open: clr
  Register #(.width(32)) Reg17 (.D(WrData), .en(WrReg17), .Q(RegData17), .clk(Clock));  // open: clr
  Register #(.width(32)) Reg21 (.D(WrData), .en(WrReg21), .Q(RegData21), .clk(Clock));  // open: clr
  Register #(.width(32)) Reg25 (.D(WrData), .en(WrReg25), .Q(RegData25), .clk(Clock));  // open: clr
  Register #(.width(32)) Reg29 (.D(WrData), .en(WrReg29), .Q(RegData29), .clk(Clock));  // open: clr
  // Probe on RegData1
  // Probe on RegData5
  // Probe on RegData9
  // Probe on RegData13
  // Probe on RegData17
  // Probe on RegData21
  // Probe on RegData25
  // Probe on RegData29
  // Probe on RegData2
  Register #(.width(32)) Reg2 (.D(WrData), .en(WrReg2), .Q(RegData2), .clk(Clock));  // open: clr
  // Probe on RegData6
  Register #(.width(32)) Reg6 (.D(WrData), .en(WrReg6), .Q(RegData6), .clk(Clock));  // open: clr
  // Probe on RegData10
  Register #(.width(32)) Reg10 (.D(WrData), .en(WrReg10), .Q(RegData10), .clk(Clock));  // open: clr
  // Probe on RegData14
  Register #(.width(32)) Reg14 (.D(WrData), .en(WrReg14), .Q(RegData14), .clk(Clock));  // open: clr
  // Probe on RegData18
  Register #(.width(32)) Reg18 (.D(WrData), .en(WrReg18), .Q(RegData18), .clk(Clock));  // open: clr
  // Probe on RegData22
  Register #(.width(32)) Reg22 (.D(WrData), .en(WrReg22), .Q(RegData22), .clk(Clock));  // open: clr
  // Probe on RegData26
  Register #(.width(32)) Reg26 (.D(WrData), .en(WrReg26), .Q(RegData26), .clk(Clock));  // open: clr
  // Probe on RegData30
  Register #(.width(32)) Reg30 (.D(WrData), .en(WrReg30), .Q(RegData30), .clk(Clock));  // open: clr
  // Probe on RegData3
  Register #(.width(32)) Reg3 (.D(WrData), .en(WrReg3), .Q(RegData3), .clk(Clock));  // open: clr
  // Probe on RegData7
  Register #(.width(32)) Reg7 (.D(WrData), .en(WrReg7), .Q(RegData7), .clk(Clock));  // open: clr
  // Probe on RegData11
  Register #(.width(32)) Reg11 (.D(WrData), .en(WrReg11), .Q(RegData11), .clk(Clock));  // open: clr
  // Probe on RegData15
  Register #(.width(32)) Reg15 (.D(WrData), .en(WrReg15), .Q(RegData15), .clk(Clock));  // open: clr
  // Probe on RegData19
  Register #(.width(32)) Reg19 (.D(WrData), .en(WrReg19), .Q(RegData19), .clk(Clock));  // open: clr
  // Probe on RegData23
  Register #(.width(32)) Reg23 (.D(WrData), .en(WrReg23), .Q(RegData23), .clk(Clock));  // open: clr
  // Probe on RegData27
  Register #(.width(32)) Reg27 (.D(WrData), .en(WrReg27), .Q(RegData27), .clk(Clock));  // open: clr
  // Probe on RegData31
  Register #(.width(32)) Reg31 (.D(WrData), .en(WrReg31), .Q(RegData31), .clk(Clock));  // open: clr
  Multiplexer #(.select(5), .width(32), .enable("false")) multiplexer_1 (
    .in0({32{1'b0}}), .in1(RegData1), .in2(RegData2), .in3(RegData3), .in4(RegData4), .in5(RegData5),
    .in6(RegData6), .in7(RegData7), .in8(RegData8), .in9(RegData9), .in10(RegData10), .in11(RegData11),
    .in12(RegData12), .in13(RegData13), .in14(RegData14), .in15(RegData15), .in16(RegData16),
    .in17(RegData17), .in18(RegData18), .in19(RegData19), .in20(RegData20), .in21(RegData21),
    .in22(RegData22), .in23(RegData23), .in24(RegData24), .in25(RegData25), .in26(RegData26),
    .in27(RegData27), .in28(RegData28), .in29(RegData29), .in30(RegData30), .in31(RegData31),
    .out(multiplexer_1_out), .sel(RdAddr1));
  Multiplexer #(.select(5), .width(32), .enable("false")) multiplexer_2 (
    .in0({32{1'b0}}), .in1(RegData1), .in2(RegData2), .in3(RegData3), .in4(RegData4), .in5(RegData5),
    .in6(RegData6), .in7(RegData7), .in8(RegData8), .in9(RegData9), .in10(RegData10), .in11(RegData11),
    .in12(RegData12), .in13(RegData13), .in14(RegData14), .in15(RegData15), .in16(RegData16),
    .in17(RegData17), .in18(RegData18), .in19(RegData19), .in20(RegData20), .in21(RegData21),
    .in22(RegData22), .in23(RegData23), .in24(RegData24), .in25(RegData25), .in26(RegData26),
    .in27(RegData27), .in28(RegData28), .in29(RegData29), .in30(RegData30), .in31(RegData31),
    .out(multiplexer_2_out), .sel(RdAddr2));
  Multiplexer #(.width(32), .enable("false")) multiplexer_3 (
    .in0(multiplexer_1_out), .in1(WrData), .out(RdData1), .sel(and_1_out));
  Multiplexer #(.width(32), .enable("false")) multiplexer_4 (
    .in0(multiplexer_2_out), .in1(WrData), .out(RdData2), .sel(and_2_out));
  Comparator #(.width(5), .mode("unsigned")) comparator_1 (
    .a(WrAddr), .b(RdAddr1), .eq(comparator_1_eq));  // open: gt, lt
  and and_1 (and_1_out, comparator_1_eq, WrReg, not_1_out);
  Comparator #(.width(5), .mode("unsigned")) comparator_2 (
    .a(WrAddr), .b(RdAddr2), .eq(comparator_2_eq));  // open: gt, lt
  and and_2 (and_2_out, comparator_2_eq, WrReg, not_2_out);
  Comparator #(.width(5), .mode("unsigned")) comparator_3 (
    .a(WrAddr), .b({5{1'b0}}), .eq(comparator_3_eq));  // open: gt, lt
  not not_1 (not_1_out, comparator_3_eq);
  Comparator #(.width(5), .mode("unsigned")) comparator_4 (
    .a(WrAddr), .b({5{1'b0}}), .eq(comparator_4_eq));  // open: gt, lt
  not not_2 (not_2_out, comparator_4_eq);
endmodule

module Overflow_Unit (
  input  Add,
  input  Sub,
  input  ASign,
  input  BSign,
  input  ResultSign,
  output Overflow
);

  wire and_1_out, and_2_out, or_1_out, xnor_1_out, xor_1_out, xor_2_out;

  xnor xnor_1 (xnor_1_out, ASign, BSign);
  xor xor_1 (xor_1_out, ASign, BSign);
  and and_1 (and_1_out, xnor_1_out, Add);
  and and_2 (and_2_out, xor_1_out, Sub);
  or or_1 (or_1_out, and_1_out, and_2_out);
  xor xor_2 (xor_2_out, ResultSign, ASign);
  and and_3 (Overflow, or_1_out, xor_2_out);

  // Notes on the sheet:
  //   Overflow occurs when doing addition and sign(A) == sign(B) && sign(result) != sign(A)
  //   Or
  //   Overflow occurs when doing subtraction and sign(A) != sign(B) && sign(result) != sign(A)
endmodule

module IF_ID (
  input  Clock,
  input  notNOP,
  input  [31:0] PC,
  input  [31:0] IRin,
  input  Squish,
  output [31:0] PC_2,
  output [31:0] IRout,
  output Squish_2
);

  Register #(.width(32)) u_PC (.D(PC), .en(notNOP), .Q(PC_2), .clk(Clock));  // open: clr
  Register #(.width(32)) IR (.D(IRin), .en(notNOP), .Q(IRout), .clk(Clock));  // open: clr
  Register #(.width(1)) u_Squish (.D(Squish), .Q(Squish_2), .clk(Clock));  // open: en, clr
endmodule

module ID_EX (
  input  Clock,
  input  ALUOp3,
  input  ALUOp2,
  input  ALUOp1,
  input  ALUOp0,
  input  RegDest,
  input  Jump,
  input  Branch,
  input  MemRead,
  input  MemtoReg,
  input  MemWrite,
  input  ALUSrc,
  input  RegWrite,
  input  JR,
  input  JAL,
  input  [31:0] PC_d,
  input  [31:0] RD1,
  input  [31:0] RD1_2,
  input  [31:0] Imm,
  input  [4:0] _16_20,
  input  [4:0] _11_15,
  input  [4:0] _6_10,
  input  [4:0] _21_25,
  input  [25:0] _0_25,
  output ALUOp3_2,
  output ALUOp2_2,
  output ALUOp1_2,
  output ALUOp0_2,
  output RegDest_2,
  output Jump_2,
  output Branch_2,
  output MemRead_2,
  output MemtoReg_2,
  output MemWrite_2,
  output ALUSrc_2,
  output RegWrite_2,
  output JR_2,
  output JAL_2,
  output [31:0] PC,
  output [31:0] A,
  output [31:0] B,
  output [31:0] Imm_2,
  output [4:0] _16_20_2,
  output [4:0] _11_15_2,
  output [4:0] shift,
  output [4:0] RS,
  output [25:0] _0_25_2
);

  Register #(.width(1)) register_1 (.D(ALUOp3), .Q(ALUOp3_2), .clk(Clock));  // open: en, clr
  Register #(.width(1)) register_2 (.D(ALUOp2), .Q(ALUOp2_2), .clk(Clock));  // open: en, clr
  Register #(.width(1)) register_3 (.D(ALUOp1), .Q(ALUOp1_2), .clk(Clock));  // open: en, clr
  Register #(.width(1)) register_4 (.D(ALUOp0), .Q(ALUOp0_2), .clk(Clock));  // open: en, clr
  Register #(.width(1)) register_5 (.D(RegDest), .Q(RegDest_2), .clk(Clock));  // open: en, clr
  Register #(.width(1)) register_6 (.D(Jump), .Q(Jump_2), .clk(Clock));  // open: en, clr
  Register #(.width(1)) register_7 (.D(Branch), .Q(Branch_2), .clk(Clock));  // open: en, clr
  Register #(.width(1)) register_8 (.D(MemRead), .Q(MemRead_2), .clk(Clock));  // open: en, clr
  Register #(.width(1)) register_9 (.D(MemtoReg), .Q(MemtoReg_2), .clk(Clock));  // open: en, clr
  Register #(.width(1)) register_10 (.D(MemWrite), .Q(MemWrite_2), .clk(Clock));  // open: en, clr
  Register #(.width(1)) register_11 (.D(ALUSrc), .Q(ALUSrc_2), .clk(Clock));  // open: en, clr
  Register #(.width(1)) register_12 (.D(RegWrite), .Q(RegWrite_2), .clk(Clock));  // open: en, clr
  Register #(.width(1)) register_13 (.D(JR), .Q(JR_2), .clk(Clock));  // open: en, clr
  Register #(.width(1)) register_14 (.D(JAL), .Q(JAL_2), .clk(Clock));  // open: en, clr
  Register #(.width(32)) register_15 (.D(PC_d), .Q(PC), .clk(Clock));  // open: en, clr
  Register #(.width(32)) register_16 (.D(RD1), .Q(A), .clk(Clock));  // open: en, clr
  Register #(.width(32)) register_17 (.D(RD1_2), .Q(B), .clk(Clock));  // open: en, clr
  Register #(.width(32)) register_18 (.D(Imm), .Q(Imm_2), .clk(Clock));  // open: en, clr
  Register #(.width(5)) register_19 (.D(_16_20), .Q(_16_20_2), .clk(Clock));  // open: en, clr
  Register #(.width(5)) register_20 (.D(_11_15), .Q(_11_15_2), .clk(Clock));  // open: en, clr
  Register #(.width(5)) register_21 (.D(_6_10), .Q(shift), .clk(Clock));  // open: en, clr
  Register #(.width(5)) register_22 (.D(_21_25), .Q(RS), .clk(Clock));  // open: en, clr
  Register #(.width(26)) register_23 (.D(_0_25), .Q(_0_25_2), .clk(Clock));  // open: en, clr
endmodule

module EX_MEM (
  input  Clock,
  input  ALUOp3,
  input  ALUOp2,
  input  ALUOp1,
  input  ALUOp0,
  input  RegDest,
  input  Jump,
  input  Branch,
  input  MemRead,
  input  MemtoReg,
  input  MemWrite,
  input  ALUSrc,
  input  RegWrite,
  input  JR,
  input  JAL,
  input  [31:0] PC,
  input  [31:0] ALU,
  input  [31:0] RD,
  input  zero,
  input  [4:0] dest,
  output ALUOp3_2,
  output ALUOp2_2,
  output ALUOp1_2,
  output ALUOp0_2,
  output RegDest_2,
  output Jump_2,
  output Branch_2,
  output MemRead_2,
  output MemtoReg_2,
  output MemWrite_2,
  output ALUSrc_2,
  output RegWrite_2,
  output JR_2,
  output JAL_2,
  output [31:0] PC_2,
  output [31:0] ALU_2,
  output [31:0] RD_2,
  output zero_2,
  output [4:0] dest_2
);

  Register #(.width(1)) register_1 (.D(ALUOp3), .Q(ALUOp3_2), .clk(Clock));  // open: en, clr
  Register #(.width(1)) register_2 (.D(ALUOp2), .Q(ALUOp2_2), .clk(Clock));  // open: en, clr
  Register #(.width(1)) register_3 (.D(ALUOp1), .Q(ALUOp1_2), .clk(Clock));  // open: en, clr
  Register #(.width(1)) register_4 (.D(ALUOp0), .Q(ALUOp0_2), .clk(Clock));  // open: en, clr
  Register #(.width(1)) register_5 (.D(RegDest), .Q(RegDest_2), .clk(Clock));  // open: en, clr
  Register #(.width(1)) register_6 (.D(Jump), .Q(Jump_2), .clk(Clock));  // open: en, clr
  Register #(.width(1)) register_7 (.D(Branch), .Q(Branch_2), .clk(Clock));  // open: en, clr
  Register #(.width(1)) register_8 (.D(MemRead), .Q(MemRead_2), .clk(Clock));  // open: en, clr
  Register #(.width(1)) register_9 (.D(MemtoReg), .Q(MemtoReg_2), .clk(Clock));  // open: en, clr
  Register #(.width(1)) register_10 (.D(MemWrite), .Q(MemWrite_2), .clk(Clock));  // open: en, clr
  Register #(.width(1)) register_11 (.D(ALUSrc), .Q(ALUSrc_2), .clk(Clock));  // open: en, clr
  Register #(.width(1)) register_12 (.D(RegWrite), .Q(RegWrite_2), .clk(Clock));  // open: en, clr
  Register #(.width(1)) register_13 (.D(JR), .Q(JR_2), .clk(Clock));  // open: en, clr
  Register #(.width(1)) register_14 (.D(JAL), .Q(JAL_2), .clk(Clock));  // open: en, clr
  Register #(.width(32)) register_15 (.D(PC), .Q(PC_2), .clk(Clock));  // open: en, clr
  Register #(.width(32)) register_16 (.D(ALU), .Q(ALU_2), .clk(Clock));  // open: en, clr
  Register #(.width(32)) register_17 (.D(RD), .Q(RD_2), .clk(Clock));  // open: en, clr
  Register #(.width(1)) register_18 (.D(zero), .Q(zero_2), .clk(Clock));  // open: en, clr
  Register #(.width(5)) register_19 (.D(dest), .Q(dest_2), .clk(Clock));  // open: en, clr
endmodule

module MEM_WB (
  input  Clock,
  input  ALUOp3,
  input  ALUOp2,
  input  ALUOp1,
  input  ALUOp0,
  input  RegDest,
  input  Jump,
  input  Branch,
  input  MemRead,
  input  MemtoReg,
  input  MemWrite,
  input  ALUSrc,
  input  RegWrite,
  input  JR,
  input  JAL,
  input  [31:0] Data,
  input  [31:0] ALU,
  input  [4:0] WrAddr,
  output ALUOp3_2,
  output ALUOp2_2,
  output ALUOp1_2,
  output ALUOp0_2,
  output RegDest_2,
  output Jump_2,
  output Branch_2,
  output MemRead_2,
  output MemtoReg_2,
  output MemWrite_2,
  output ALUSrc_2,
  output RegWrite_2,
  output JR_2,
  output JAL_2,
  output [31:0] Data_2,
  output [31:0] ALU_2,
  output [4:0] WrAddr_2
);

  Register #(.width(1)) register_1 (.D(ALUOp3), .Q(ALUOp3_2), .clk(Clock));  // open: en, clr
  Register #(.width(1)) register_2 (.D(ALUOp2), .Q(ALUOp2_2), .clk(Clock));  // open: en, clr
  Register #(.width(1)) register_3 (.D(ALUOp1), .Q(ALUOp1_2), .clk(Clock));  // open: en, clr
  Register #(.width(1)) register_4 (.D(ALUOp0), .Q(ALUOp0_2), .clk(Clock));  // open: en, clr
  Register #(.width(1)) register_5 (.D(RegDest), .Q(RegDest_2), .clk(Clock));  // open: en, clr
  Register #(.width(1)) register_6 (.D(Jump), .Q(Jump_2), .clk(Clock));  // open: en, clr
  Register #(.width(1)) register_7 (.D(Branch), .Q(Branch_2), .clk(Clock));  // open: en, clr
  Register #(.width(1)) register_8 (.D(MemRead), .Q(MemRead_2), .clk(Clock));  // open: en, clr
  Register #(.width(1)) register_9 (.D(MemtoReg), .Q(MemtoReg_2), .clk(Clock));  // open: en, clr
  Register #(.width(1)) register_10 (.D(MemWrite), .Q(MemWrite_2), .clk(Clock));  // open: en, clr
  Register #(.width(1)) register_11 (.D(ALUSrc), .Q(ALUSrc_2), .clk(Clock));  // open: en, clr
  Register #(.width(1)) register_12 (.D(RegWrite), .Q(RegWrite_2), .clk(Clock));  // open: en, clr
  Register #(.width(1)) register_13 (.D(JR), .Q(JR_2), .clk(Clock));  // open: en, clr
  Register #(.width(1)) register_14 (.D(JAL), .Q(JAL_2), .clk(Clock));  // open: en, clr
  Register #(.width(32)) register_15 (.D(Data), .Q(Data_2), .clk(Clock));  // open: en, clr
  Register #(.width(32)) register_16 (.D(ALU), .Q(ALU_2), .clk(Clock));  // open: en, clr
  Register #(.width(5)) register_17 (.D(WrAddr), .Q(WrAddr_2), .clk(Clock));  // open: en, clr
endmodule

module Control_Unit (
  input  [5:0] OpCode,
  input  [5:0] Func,
  output [13:0] Flags
);

  ROM #(.addrWidth(12), .dataWidth(14)) rom_1 (.addr({OpCode, Func}), .data(Flags));  // open: sel

  // Notes on the sheet:
  //   contents of rom_1 (hex, n*v repeats v):
  //   3c04 4 3804 5*4 204 23*4 c04 4 1004 4 1804 4 1404 4 4 4 804 404 20*4 192*0 64*208 192*0 64*e0c 192*0
  //   64*1a0c 64*20c 1344*0 64*e6c 448*0 64*218
endmodule

module Hazard_Detection (
  input  ID_EX_MemRead,
  input  [4:0] ID_EX_Rt,
  input  [4:0] IF_ID_Rs,
  input  [4:0] IF_ID_Rt,
  input  MemWrite_Dec,
  output IF_ID_Write,
  output PCWrite,
  output Stall_Control,
  output Stalling
);

  wire and_1_out, comparator_1_eq, comparator_2_eq, or_1_out;

  Comparator #(.width(5)) comparator_1 (.a(ID_EX_Rt), .b(IF_ID_Rs), .eq(comparator_1_eq));  // open: gt, lt
  Comparator #(.width(5)) comparator_2 (.a(ID_EX_Rt), .b(IF_ID_Rt), .eq(comparator_2_eq));  // open: gt, lt
  and and_1 (and_1_out, comparator_2_eq, MemWrite_Dec);
  or or_1 (or_1_out, comparator_1_eq, and_1_out);
  and and_2 (Stall_Control, ID_EX_MemRead, or_1_out);
  not not_1 (IF_ID_Write, Stall_Control);

  assign PCWrite = IF_ID_Write;
  assign Stalling = Stall_Control;
endmodule

// Forward Unit
module Forwarding_Unit (
  input  [4:0] ID_EX_Rs,
  input  [4:0] ID_EX_Rt,
  input  EX_MEM_RegWrite,
  input  [4:0] EX_MEM_Reg_Rd,
  input  MEM_WB_RegWrite,
  input  [4:0] MEM_WB_Reg_Rd,
  input  EX_MEM_MemWrite,
  output [1:0] ForwardA,
  output [1:0] ForwardB,
  output MemForward
);

  wire comparator_1_eq, comparator_2_eq, comparator_3_eq, comparator_4_eq, comparator_5_eq, comparator_6_eq,
       comparator_7_eq, comparator_8_eq, comparator_9_eq, not_1_out, not_2_out, not_3_out, not_4_out,
       not_5_out, not_6_out;

  Comparator #(.width(5)) comparator_1 (.a(EX_MEM_Reg_Rd), .b({5{1'b0}}), .eq(comparator_1_eq));  // open: gt, lt
  not not_1 (not_1_out, comparator_1_eq);
  Comparator #(.width(5)) comparator_2 (.a(EX_MEM_Reg_Rd), .b(ID_EX_Rs), .eq(comparator_2_eq));  // open: gt, lt
  Comparator #(.width(5)) comparator_3 (.a(ID_EX_Rs), .b(MEM_WB_Reg_Rd), .eq(comparator_3_eq));  // open: gt, lt
  Comparator #(.width(5)) comparator_4 (.a(MEM_WB_Reg_Rd), .b({5{1'b0}}), .eq(comparator_4_eq));  // open: gt, lt
  not not_2 (not_2_out, comparator_4_eq);
  Comparator #(.width(5)) comparator_5 (.a(EX_MEM_Reg_Rd), .b(ID_EX_Rt), .eq(comparator_5_eq));  // open: gt, lt
  Comparator #(.width(5)) comparator_6 (.a(EX_MEM_Reg_Rd), .b({5{1'b0}}), .eq(comparator_6_eq));  // open: gt, lt
  not not_3 (not_3_out, comparator_6_eq);
  Comparator #(.width(5)) comparator_7 (.a(MEM_WB_Reg_Rd), .b(ID_EX_Rt), .eq(comparator_7_eq));  // open: gt, lt
  not not_4 (not_4_out, comparator_8_eq);
  Comparator #(.width(5)) comparator_8 (.a(MEM_WB_Reg_Rd), .b({5{1'b0}}), .eq(comparator_8_eq));  // open: gt, lt
  Comparator #(.width(5)) comparator_9 (.a(MEM_WB_Reg_Rd), .b(EX_MEM_Reg_Rd), .eq(comparator_9_eq));  // open: gt, lt
  and and_1 (ForwardA[1], EX_MEM_RegWrite, not_1_out, comparator_2_eq);
  not not_5 (not_5_out, ForwardA[1]);
  and and_2 (ForwardA[0], not_5_out, MEM_WB_RegWrite, comparator_3_eq, not_2_out);
  and and_3 (ForwardB[1], EX_MEM_RegWrite, comparator_5_eq, not_3_out);
  not not_6 (not_6_out, ForwardB[1]);
  and and_4 (ForwardB[0], not_6_out, comparator_7_eq, not_4_out, MEM_WB_RegWrite);
  and and_5 (MemForward, not_4_out, comparator_9_eq, MEM_WB_RegWrite, EX_MEM_MemWrite);
endmodule
